# Fritzing sketch uno_dht11 (saved by Fritzing 0.9.2b)

parts:
  Arduino_UNO = Arduino Uno (Rev3)
  DHT11 = DHT11 Humitidy and Temperature Sensor
  R1 = Resistor [tolerance=±5% resistance=4.7k package=THT]

nets:
  GND: Arduino_UNO.GND, DHT11.GND
  N1: Arduino_UNO.D2, DHT11.DATA, R1.Pin_1
  5V: Arduino_UNO.5V, DHT11.VDD, R1.Pin_0

custom parts:
  DHT11 Humitidy and Temperature Sensor: DHT11 Humidity and Temperature Sensor
