# Fritzing sketch uno_DFhx711_load_cell_ v1_1 (saved by Fritzing 0.9.2b)

parts:
  Arduino_UNO = Arduino Uno (Rev3)
  Εξάρτημα1 = dfHX711 Weighing Sensor Module

nets:
  N1: Arduino_UNO.A3, Εξάρτημα1.SCK
  N2: Arduino_UNO.A4/SDA, Εξάρτημα1.DOUT
  5V: Arduino_UNO.5V, Εξάρτημα1.VCC
  GND: Arduino_UNO.GND, Εξάρτημα1.GND

notes:
  To load cell

custom parts:
  dfHX711 Weighing Sensor Module: HX711 is a precision 24-bit analog-to-digital converter (ADC) designed for weigh scales and industrial control applications to interface directly with a bridge sensor.
