# Fritzing sketch sd_card (saved by Fritzing 0.9.2b)
breadboards: 1

parts:
  IC1 = IC, DIP package, 16 pins [chip_label=74HC4050]
  Arduino1 = Arduino Uno (Rev3)
  Εξάρτημα1 = prefix00001rb

nets:
  N1: IC1.pin1, Arduino1.3V3
  N2: IC1.pin8, Arduino1.GND, Εξάρτημα1.connector0, Εξάρτημα1.connector7, Εξάρτημα1.connector8, Εξάρτημα1.connector15
  N3: IC1.pin9, Arduino1.D13/SCK
  N4: IC1.pin10, Εξάρτημα1.connector5, Εξάρτημα1.connector13
  N5: IC1.pin11, Arduino1.D11_PWM/MOSI
  N6: IC1.pin12, Εξάρτημα1.connector4, Εξάρτημα1.connector12
  N7: IC1.pin14, Arduino1.D4
  N8: IC1.pin15, Εξάρτημα1.connector3, Εξάρτημα1.connector11
  N9: Arduino1.D12/MISO, Εξάρτημα1.connector6, Εξάρτημα1.connector14
  N10: Arduino1.5V, Εξάρτημα1.connector2, Εξάρτημα1.connector10
